// Logisim project additionneur.circ as structural Verilog: 4 circuits, main circuit main
module main (
);


  // Notes on the sheet:
  //   Création d'un additionneur
  //   1) Demi-additionneur
  //   2) Additionneur complet
  //   3) Additionneur 4 bits
endmodule

module DemiAdd (
  input  A,
  input  B,
  output Res,
  output Ret
);

  xor xor_1 (Res, A, B);
  and and_1 (Ret, A, B);
endmodule

module Add (
  input  A,
  input  B,
  input  C,
  output Res,
  output Ret
);

  wire demiadd_1_res, demiadd_1_ret, demiadd_2_ret;

  DemiAdd demiadd_1 (.A(A), .B(B), .Res(demiadd_1_res), .Ret(demiadd_1_ret));
  DemiAdd demiadd_2 (.A(demiadd_1_res), .B(C), .Res(Res), .Ret(demiadd_2_ret));
  or or_1 (Ret, demiadd_2_ret, demiadd_1_ret);
endmodule

module Add4 (
  input  RetE,
  input  A0,
  input  B0,
  input  A1,
  input  B1,
  input  A2,
  input  B2,
  input  A3,
  input  B3,
  output Res0,
  output Res1,
  output Res2,
  output Res3,
  output RetS
);

  wire add_1_ret, add_2_ret, add_3_ret;

  Add add_1 (.A(A0), .B(B0), .C(RetE), .Res(Res0), .Ret(add_1_ret));
  Add add_2 (.A(A1), .B(B1), .C(add_1_ret), .Res(Res1), .Ret(add_2_ret));
  Add add_3 (.A(A2), .B(B2), .C(add_2_ret), .Res(Res2), .Ret(add_3_ret));
  Add add_4 (.A(A3), .B(B3), .C(add_3_ret), .Res(Res3), .Ret(RetS));
endmodule
