// Logisim project euclide.circ as structural Verilog: 1 circuit, main circuit main
module main (
  input  in_1
);

  wire comparator_1_gt, not_1_out;
  wire [7:0] A_q, B_q, multiplexer_1_out, multiplexer_2_out, subtractor_1_out, subtractor_2_out;

  Register A (.D(multiplexer_1_out), .Q(A_q), .clk(in_1));  // open: en, clr
  Register B (.D(multiplexer_2_out), .Q(B_q), .clk(in_1));  // open: en, clr
  Comparator comparator_1 (.a(A_q), .b(B_q), .gt(comparator_1_gt));  // open: eq, lt
  Subtractor subtractor_1 (.a(A_q), .b(B_q), .out(subtractor_1_out));  // open: bin, bout
  Subtractor subtractor_2 (.a(B_q), .b(A_q), .out(subtractor_2_out));  // open: bin, bout
  not not_1 (not_1_out, comparator_1_gt);
  Multiplexer #(.width(8)) multiplexer_1 (
    .in0(A_q), .in1(subtractor_1_out), .out(multiplexer_1_out), .sel(comparator_1_gt));  // open: en
  Multiplexer #(.width(8)) multiplexer_2 (
    .in0(B_q), .in1(subtractor_2_out), .out(multiplexer_2_out), .sel(not_1_out));  // open: en

  // Notes on the sheet:
  //   Algorithme d'Euclide
endmodule
